// Logisim project Display 3.circ as structural Verilog: 1 circuit, main circuit main
module main (
  input  C,
  input  D,
  input  B,
  input  A
);

  wire and_1_out, and_2_out, and_3_out, nand_1_out, nand_2_out, nand_3_out, nand_4_out, not_1_out, not_2_out,
       not_3_out, not_4_out, not_5_out, or_1_out, or_2_out, or_3_out, or_4_out, or_5_out, or_6_out, or_7_out,
       or_8_out, or_9_out, or_10_out, or_11_out, or_12_out, or_13_out, or_14_out, or_15_out, or_16_out,
       S___0_2_out, S___0_3_out, S___0_out, S___1_2_out, S___1_3_out, S___1_out, S___U_out, T___0_2_out,
       T___0_3_out, T___0_out, T___1_2_out, T___1_3_out, T___1_out, T_out, V___0_2_out, V___0_3_out,
       V___0_out, V___1_2_out, V___1_3_out, V___1_out, V_out, W___0_2_out, W___0_3_out, W___0_out,
       W___1_2_out, W___1_3_out, W___1_out, W_out, X___0_2_out, X___0_3_out, X___0_out, X___1_2_out,
       X___1_3_out, X___1_out, X_out, xnor_1_out, xor_1_out, Y___0_2_out, Y___0_3_out, Y___0_out,
       Y___1_2_out, Y___1_3_out, Y___1_out, Y_out;

  not not_1 (not_1_out, C);
  not not_2 (not_2_out, D);
  or or_1 (or_1_out, C, not_2_out);
  or or_2 (or_2_out, C, D);
  xnor xnor_1 (xnor_1_out, C, D);
  nand nand_1 (nand_1_out, C, not_2_out);
  not not_3 (not_3_out, or_2_out);
  and and_1 (and_1_out, not_1_out, not_2_out);
  xor xor_1 (xor_1_out, B, D);
  and and_2 (and_2_out, not_1_out, D);
  nand nand_2 (nand_2_out, C, D);
  and and_3 (and_3_out, C, C);
  nand nand_3 (nand_3_out, C, D);
  nand nand_4 (nand_4_out, C, not_2_out);
  or or_3 (or_3_out, C, not_2_out);
  or or_4 (or_4_out, C, D);
  not not_4 (not_4_out, B);
  and S___0 (S___0_out, or_1_out, not_4_out);
  and S___1 (S___1_out, B, xnor_1_out);
  and S___0_2 (S___0_2_out, not_4_out, nand_1_out);
  and S___1_2 (S___1_2_out, or_1_out, B);
  and T___0 (T___0_out, C, not_4_out);
  and T___1 (T___1_out, or_2_out, B);
  and T___0_2 (T___0_2_out, not_4_out, not_4_out);
  and T___1_2 (T___1_2_out, B, B);
  and V___0 (V___0_out, not_3_out, not_4_out);
  and V___1 (V___1_out, and_1_out, B);
  and V___0_2 (V___0_2_out, not_1_out, not_4_out);
  and V___1_2 (V___1_2_out, C, B);
  and W___0 (W___0_out, xor_1_out, not_4_out);
  and W___1 (W___1_out, and_2_out, B);
  and W___0_2 (W___0_2_out, nand_2_out, not_4_out);
  and W___1_2 (W___1_2_out, and_3_out, B);
  and X___0 (X___0_out, not_4_out, not_4_out);
  and X___1 (X___1_out, not_4_out, B);
  and X___0_2 (X___0_2_out, nand_3_out, not_4_out);
  and X___1_2 (X___1_2_out, not_1_out, B);
  and Y___0 (Y___0_out, nand_4_out, not_4_out);
  and Y___1 (Y___1_out, or_3_out, B);
  and Y___0_2 (Y___0_2_out, or_4_out, not_4_out);
  and Y___1_2 (Y___1_2_out, B, B);
  or or_5 (or_5_out, Y___0_2_out, Y___1_2_out);
  or or_6 (or_6_out, S___0_out, S___1_out);
  or or_7 (or_7_out, S___0_2_out, S___1_2_out);
  or or_8 (or_8_out, T___0_out, T___1_out);
  or or_9 (or_9_out, T___0_2_out, T___1_2_out);
  or or_10 (or_10_out, V___0_out, V___1_out);
  or or_11 (or_11_out, V___0_2_out, V___1_2_out);
  or or_12 (or_12_out, W___0_out, W___1_out);
  or or_13 (or_13_out, W___0_2_out, W___1_2_out);
  or or_14 (or_14_out, X___0_out, X___1_out);
  or or_15 (or_15_out, X___0_2_out, X___1_2_out);
  or or_16 (or_16_out, Y___0_out, Y___1_out);
  not not_5 (not_5_out, A);
  and X___0_3 (X___0_3_out, or_14_out, not_5_out);
  and S___0_3 (S___0_3_out, not_5_out, or_6_out);
  and S___1_3 (S___1_3_out, A, or_7_out);
  and T___0_3 (T___0_3_out, or_8_out, not_5_out);
  and T___1_3 (T___1_3_out, or_9_out, A);
  and V___0_3 (V___0_3_out, or_10_out, not_5_out);
  and V___1_3 (V___1_3_out, or_11_out, A);
  and W___0_3 (W___0_3_out, or_12_out, not_5_out);
  and W___1_3 (W___1_3_out, or_13_out, A);
  and X___1_3 (X___1_3_out, or_15_out, A);
  and Y___0_3 (Y___0_3_out, or_16_out, not_5_out);
  and Y___1_3 (Y___1_3_out, or_5_out, A);
  or S___U (S___U_out, S___0_3_out, S___1_3_out);
  or T (T_out, T___0_3_out, T___1_3_out);
  or V (V_out, V___0_3_out, V___1_3_out);
  or W (W_out, W___0_3_out, W___1_3_out);
  or X (X_out, X___0_3_out, X___1_3_out);
  or Y (Y_out, Y___0_3_out, Y___1_3_out);
  _7_Segment_Display u_7_segment_display_1 (
    .g(W_out), .f(V_out), .a(T_out), .b(S___U_out), .e(Y_out));  // open: d, c, dp
endmodule
